// Logisim project JK_flip_flop_corrected.circ as structural Verilog: 1 circuit, main circuit main
module main (
  input  J,
  input  K,
  input  CLR,
  output Q,
  output Qbar
);

  wire CLK_out, nand_1_out, nand_2_out, nand_3_out, nand_4_out, nand_5_out, nand_6_out, not_1_out, not_2_out;

  Clock CLK (.out(CLK_out));
  not not_1 (not_1_out, CLK_out);
  nand nand_1 (nand_1_out, Qbar, J, not_1_out);
  nand nand_2 (nand_2_out, Q, K, not_1_out);
  not not_2 (not_2_out, not_1_out);
  nand nand_3 (nand_3_out, nand_1_out, nand_4_out);
  nand nand_4 (nand_4_out, nand_3_out, CLR, nand_2_out);
  nand nand_5 (nand_5_out, nand_3_out, not_2_out);
  nand nand_6 (nand_6_out, nand_4_out, not_2_out);
  nand nand_7 (Q, nand_5_out, Qbar);
  nand nand_8 (Qbar, Q, nand_6_out);
endmodule
