// Logisim project D_flip_flop.circ as structural Verilog: 1 circuit, main circuit main
module main (
  input  D,
  output Q,
  output Qbar
);

  wire CLK_out, nand_1_out, nand_2_out, nand_3_out, nand_4_out, nand_5_out, nand_6_out, not_1_out, not_2_out,
       not_3_out, not_4_out;

  Clock CLK (.out(CLK_out));
  not not_1 (not_1_out, CLK_out);
  not not_2 (not_2_out, D);
  nand nand_1 (nand_1_out, D, not_1_out);
  nand nand_2 (nand_2_out, not_1_out, not_2_out);
  nand nand_3 (nand_3_out, nand_1_out, nand_4_out);
  nand nand_4 (nand_4_out, nand_3_out, nand_2_out);
  not not_3 (not_3_out, not_1_out);
  not not_4 (not_4_out, nand_3_out);
  nand nand_5 (nand_5_out, nand_3_out, not_3_out);
  nand nand_6 (nand_6_out, not_3_out, not_4_out);
  nand nand_7 (Q, nand_5_out, Qbar);
  nand nand_8 (Qbar, Q, nand_6_out);
endmodule
