// Logisim project D_flip_flop_Async_Set_Clear.circ as structural Verilog: 1 circuit, main circuit main
module main (
  input  D,
  input  set,
  input  clr,
  output Q,
  output Qbar
);

  wire CLK_out, nand_1_out, nand_2_out, nand_3_out, nand_4_out, nand_5_out, nand_6_out, nand_7_out,
       not_1_out, not_2_out, not_3_out, not_4_out, not_5_out;

  Clock CLK (.out(CLK_out));
  not not_1 (not_1_out, CLK_out);
  not not_2 (not_2_out, D);
  not not_3 (not_3_out, clr);
  nand nand_1 (nand_1_out, D, not_3_out, not_1_out);
  nand nand_2 (nand_2_out, not_1_out, nand_3_out, not_2_out);
  nand nand_3 (nand_3_out, set, not_3_out);
  nand nand_4 (nand_4_out, nand_1_out, nand_3_out, nand_5_out);
  nand nand_5 (nand_5_out, nand_4_out, not_3_out, nand_2_out);
  not not_4 (not_4_out, not_1_out);
  not not_5 (not_5_out, nand_4_out);
  nand nand_6 (nand_6_out, nand_4_out, not_3_out, not_4_out);
  nand nand_7 (nand_7_out, not_4_out, nand_3_out, not_5_out);
  nand nand_8 (Q, nand_6_out, nand_3_out, Qbar);
  nand nand_9 (Qbar, Q, not_3_out, nand_7_out);
endmodule
